// Logisim project alu.circ as structural Verilog: 7 circuits, main circuit 2_bits_adder
module ALU (
  input  [17:0] in_1,
  input  [17:0] in_2,
  input  [1:0] ALU_operation,
  output [17:0] out_4,
  output carry_out
);

  wire [17:0] AND_out, n18_bits_adder_1_sum, OR_out, XOR_out;

  _18_bits_adder u_18_bits_adder_1 (
    .A(in_1), .B(in_2), .carry_out(carry_out), .sum(n18_bits_adder_1_sum));  // open: carry_in
  assign AND_out = in_2 & in_1;  // AND_Gate AND, 18 bits wide
  assign OR_out = in_2 | in_1;  // OR_Gate OR, 18 bits wide
  assign XOR_out = in_1 ^ in_2;  // XOR_Gate XOR, 18 bits wide
  Multiplexer #(.select(2), .width(18), .enable("false")) multiplexer_1 (
    .in0(n18_bits_adder_1_sum), .in1(AND_out), .in2(OR_out), .in3(XOR_out), .out(out_4), .sel(ALU_operation));
endmodule

module program_counter (
  input  [17:0] \input ,
  input  en,
  input  write,
  input  clk,
  output [17:0] \output 
);

  wire [17:0] multiplexer_1_out;

  Multiplexer #(.width(18), .enable("false")) multiplexer_1 (
    .in0(\output ), .in1(\input ), .out(multiplexer_1_out), .sel(write));
  Register #(.width(18)) register_1 (.D(multiplexer_1_out), .en(en), .Q(\output ), .clk(clk), .clr(1'b0));
endmodule

module full_adder (
  input  A,
  input  B,
  input  carry_in,
  output sum,
  output carry_out
);

  wire and_1_out, and_2_out, xor_1_out;

  xor xor_1 (xor_1_out, A, B);
  xor xor_2 (sum, xor_1_out, carry_in);
  and and_1 (and_1_out, carry_in, xor_1_out);
  and and_2 (and_2_out, B, A);
  or or_1 (carry_out, and_1_out, and_2_out);
endmodule

module _2_bits_adder (
  input  [1:0] A,
  input  [1:0] B,
  input  carry_in,
  output carry_out,
  output [1:0] sum
);

  wire full_adder_1_carry_out;

  full_adder full_adder_1 (.A(A[0]), .B(B[0]), .carry_in(carry_in), .sum(sum[0]), .carry_out(full_adder_1_carry_out));
  full_adder full_adder_2 (.A(A[1]), .B(B[1]), .carry_in(full_adder_1_carry_out), .sum(sum[1]), .carry_out(carry_out));
endmodule

module _4_bits_adder (
  input  [3:0] A,
  input  [3:0] B,
  input  carry_in,
  output carry_out,
  output [3:0] sum
);

  wire full_adder_1_carry_out, full_adder_2_carry_out, full_adder_3_carry_out;

  full_adder full_adder_1 (.A(A[0]), .B(B[0]), .carry_in(carry_in), .sum(sum[0]), .carry_out(full_adder_1_carry_out));
  full_adder full_adder_2 (
    .A(A[1]), .B(B[1]), .carry_in(full_adder_1_carry_out), .sum(sum[1]), .carry_out(full_adder_2_carry_out));
  full_adder full_adder_3 (
    .A(A[2]), .B(B[2]), .carry_in(full_adder_2_carry_out), .sum(sum[2]), .carry_out(full_adder_3_carry_out));
  full_adder full_adder_4 (.A(A[3]), .B(B[3]), .carry_in(full_adder_3_carry_out), .sum(sum[3]), .carry_out(carry_out));
endmodule

module _8_bits_adder (
  input  [7:0] A,
  input  [7:0] B,
  input  carry_in,
  output carry_out,
  output [7:0] sum
);

  wire n4_bits_adder_1_carry_out;

  _4_bits_adder u_4_bits_adder_1 (
    .A(A[3:0]), .B(B[3:0]), .carry_in(carry_in), .carry_out(n4_bits_adder_1_carry_out), .sum(sum[3:0]));
  _4_bits_adder u_4_bits_adder_2 (
    .A(A[7:4]), .B(B[7:4]), .carry_in(n4_bits_adder_1_carry_out), .carry_out(carry_out), .sum(sum[7:4]));
endmodule

module _18_bits_adder (
  input  [17:0] A,
  input  [17:0] B,
  input  carry_in,
  output carry_out,
  output [17:0] sum
);

  wire n2_bits_adder_1_carry_out, n2_bits_adder_2_carry_out, n2_bits_adder_3_carry_out,
       n2_bits_adder_4_carry_out, n2_bits_adder_5_carry_out, n2_bits_adder_6_carry_out,
       n2_bits_adder_7_carry_out, n2_bits_adder_8_carry_out;

  _2_bits_adder u_2_bits_adder_1 (
    .A(A[1:0]), .B(B[1:0]), .carry_in(carry_in), .carry_out(n2_bits_adder_1_carry_out), .sum(sum[1:0]));
  _2_bits_adder u_2_bits_adder_2 (
    .A(A[3:2]), .B(B[3:2]), .carry_in(n2_bits_adder_1_carry_out), .carry_out(n2_bits_adder_2_carry_out),
    .sum(sum[3:2]));
  _2_bits_adder u_2_bits_adder_3 (
    .A(A[5:4]), .B(B[5:4]), .carry_in(n2_bits_adder_2_carry_out), .carry_out(n2_bits_adder_3_carry_out),
    .sum(sum[5:4]));
  _2_bits_adder u_2_bits_adder_4 (
    .A(A[7:6]), .B(B[7:6]), .carry_in(n2_bits_adder_3_carry_out), .carry_out(n2_bits_adder_4_carry_out),
    .sum(sum[7:6]));
  _2_bits_adder u_2_bits_adder_5 (
    .A(A[11:10]), .B(B[11:10]), .carry_in(n2_bits_adder_6_carry_out), .carry_out(n2_bits_adder_5_carry_out),
    .sum(sum[11:10]));
  _2_bits_adder u_2_bits_adder_6 (
    .A(A[9:8]), .B(B[9:8]), .carry_in(n2_bits_adder_4_carry_out), .carry_out(n2_bits_adder_6_carry_out),
    .sum(sum[9:8]));
  _2_bits_adder u_2_bits_adder_7 (
    .A(A[13:12]), .B(B[13:12]), .carry_in(n2_bits_adder_5_carry_out), .carry_out(n2_bits_adder_7_carry_out),
    .sum(sum[13:12]));
  _2_bits_adder u_2_bits_adder_8 (
    .A(A[15:14]), .B(B[15:14]), .carry_in(n2_bits_adder_7_carry_out), .carry_out(n2_bits_adder_8_carry_out),
    .sum(sum[15:14]));
  _2_bits_adder u_2_bits_adder_9 (
    .A(A[17:16]), .B(B[17:16]), .carry_in(n2_bits_adder_8_carry_out), .carry_out(carry_out), .sum(sum[17:16]));
endmodule
