// Logisim project ControlUnit.circ as structural Verilog
module ControlUnit (
  input  [19:0] in_1
);


  // Other names for the same wires on the sheet: ADDRESS10[9:0] = {in_1[0], in_1[1], in_1[2], in_1[3], in_1[4], in_1[5], in_1[6], in_1[7], in_1[8], in_1[9]};
  //   ADDRESS14[13:0] = in_1[13:0]; OP2[3:0] = in_1[9:6]; SRC1[3:0] = in_1[9:6]; ADDRESS6[5:0] = in_1[5:0];
  //   IMM[5:0] = in_1[5:0]; SRC2[3:0] = in_1[5:2]; OPCODE[3:0] = in_1[17:14]; DEST[3:0] = in_1[13:10];
  //   OP1[3:0] = in_1[13:10]; SRC[3:0] = in_1[13:10]

  // Notes on the sheet:
  //   First 2 bits are useless
endmodule
